// Logisim project Alarme.circ as structural Verilog: 1 circuit, main circuit main
module main (
  input  Ligar,
  input  Sensor
);

  wire and_1_out, and_2_out, and_3_out, and_4_out, and_5_out, and_6_out, and_7_out, clock_1_out, D0_q, D1_q,
       not_1_out, not_2_out, or_1_out, or_2_out, or_3_out, or_4_out;

  Clock clock_1 (.out(clock_1_out));
  not not_1 (not_1_out, Ligar);
  not not_2 (not_2_out, Sensor);
  and and_1 (and_1_out, D1_q, Ligar);
  and and_2 (and_2_out, Sensor, Ligar);
  and and_3 (and_3_out, Ligar, D1_q);
  and and_4 (and_4_out, Ligar, D0_q);
  and and_5 (and_5_out, not_2_out, Ligar);
  or or_1 (or_1_out, not_1_out, not_1_out);
  and and_6 (and_6_out, Ligar, Sensor);
  or or_2 (or_2_out, and_1_out, and_2_out);
  or or_3 (or_3_out, and_3_out, and_4_out, and_5_out);
  _7_Segment_Display u_7_segment_display_1 (
    .g(or_4_out), .f(or_4_out), .a(or_4_out), .b(or_4_out), .e(Ligar), .d(Ligar), .c(and_6_out));  // open: dp
  or or_4 (or_4_out, and_6_out, or_1_out);
  D_Flip_Flop D1 (.clk(clock_1_out), .D(or_2_out), .Q(D1_q));  // open: Qn, preset, en, reset
  D_Flip_Flop D0 (.clk(clock_1_out), .D(or_3_out), .Q(D0_q));  // open: Qn, preset, en, reset
  LED Alarme (.in(and_7_out));
  and and_7 (and_7_out, D1_q, D0_q);
endmodule
